# Fritzing sketch blinkColuna_03 (saved by Fritzing 0.9.3b)
breadboards: 1

parts:
  Part1 = Arduino Nano (Rev3.0) (ICSP)
  SP1 = SPEAKER [package=pcb_mount_speaker]

nets:
  N1: Part1.GND, SP1.+
  N2: Part1.D5, SP1.-
