# Fritzing sketch botaoTone_05 (saved by Fritzing 0.9.3b)
breadboards: 1

parts:
  Part1 = Arduino Nano (Rev3.0) (ICSP)
  S2 = Pushbutton [package=THT]
  R1 = Resistor [tolerance=±5% resistance=220 package="2512 [SMD]"]
  SP1 = SPEAKER [package=pcb_mount_speaker]

nets:
  N1: Part1.GND, R1.Pin_1, SP1.+
  N2: Part1.D3, SP1.-
  N3: Part1.D5, S2.leg0, R1.Pin_0
  N4: Part1.3V3, S2.leg1
