# Fritzing sketch lerBotaoDigital_04 (saved by Fritzing 0.9.3b)
breadboards: 1

parts:
  Part1 = Arduino Nano (Rev3.0) (ICSP)
  S2 = Pushbutton [package=THT]
  R1 = Resistor [tolerance=±5% resistance=220 package="2512 [SMD]"]

nets:
  N1: Part1.GND, R1.Pin_1
  N2: Part1.D5, S2.leg0, R1.Pin_0
  N3: Part1.3V3, S2.leg1
