# Fritzing sketch lerSensorAnalogico_08-01 (saved by Fritzing 0.9.3b)
breadboards: 1

parts:
  Part1 = Arduino Nano (Rev3.0) (ICSP)
  U1 = POT [package=pot_alpha_rv16af-20]
  SP1 = SPEAKER [package=pcb_mount_speaker]

nets:
  N1: Part1.GND, U1.A, SP1.+
  N2: Part1.D5, SP1.-
  N3: Part1.5V, U1.E
  N4: Part1.A0, U1.S
