# Fritzing sketch lerSensorAnalogico_08-02 (saved by Fritzing 0.9.3b)
breadboards: 1

parts:
  Part1 = Arduino Nano (Rev3.0) (ICSP)
  R1 = Photocell (LDR) [package=THT]
  R2 = Resistor [tolerance=±5% resistance=220 package="0402 [SMD]"]
  SP1 = SPEAKER [package=pcb_mount_speaker]

nets:
  N1: Part1.GND, R1.pin_0, SP1.+
  N2: Part1.D5, SP1.-
  N3: Part1.5V, R2.Pin_0
  N4: Part1.A0, R1.pin_1, R2.Pin_1
